# Fritzing sketch wearableSensorCircuit (saved by Fritzing 0.9.4)
circuit board: 16.9333cm x 5.64444cm
breadboards: 1

parts:
  R1 = Resistor [tolerance=±5% resistance=220 package=THT]
  Force_Sensor_1 = Basic Force Sensing Resistor (FSR) [package=THT]
  Force_Sensor_2 = Basic Force Sensing Resistor (FSR) [package=THT]
  R2 = Resistor [tolerance=±5% resistance=220 package=THT]
  R3 = Resistor [tolerance=±5% resistance=220 package=THT]
  Force_Sensor_3 = Basic Force Sensing Resistor (FSR) [package=THT]
  Force_Sensor_4 = Basic Force Sensing Resistor (FSR) [package=THT]
  R4 = Resistor [tolerance=±5% resistance=220 package=THT]
  part = Resistor [tolerance=±5% resistance=220 package=THT]  # not connected
  Arduino_Nano = Arduino Nano (Rev3.0)
  Battery = Battery

nets:
  N1: R1.Pin_0, R2.Pin_0, R3.Pin_0, R4.Pin_0, Arduino_Nano.GND, Battery.-
  N2: R1.Pin_1, Force_Sensor_1.pin_1, Arduino_Nano.A0
  N3: Force_Sensor_1.pin_0, Force_Sensor_2.pin_0, Force_Sensor_3.pin_0, Force_Sensor_4.pin_0, Arduino_Nano.5V
  N4: Force_Sensor_2.pin_1, R2.Pin_1, Arduino_Nano.A1
  N5: R3.Pin_1, Force_Sensor_3.pin_1, Arduino_Nano.A2
  N6: Force_Sensor_4.pin_1, R4.Pin_1, Arduino_Nano.A3
